# Fritzing sketch Arduino IR Desktop Receiver Template Circuit Diagram (saved by Fritzing 0.9.10b)
breadboards: 2

parts:
  Part1 = Arduino Pro Micro (Clone)
  IR1 = TSOP312.., 314.. [package=THT]
  Part2 = Arduino Pro Micro (Clone)
  IR2 = TSOP312.., 314.. [package=THT]
  OLED_I2C1 = OLED 128x64 I2C Monochrome Display

nets:
  GND: Part1.GND, IR1.GND
  N1: Part1.D9, IR1.Data
  N2: Part1.VCC, IR1.Vs
  GND_2: Part2.GND, IR2.GND, OLED_I2C1.GND
  N3: Part2.D2, OLED_I2C1.SCK
  N4: Part2.D3, OLED_I2C1.SDA
  N5: Part2.D9, IR2.Data
  VCC: Part2.VCC, IR2.Vs, OLED_I2C1.VDD
